// Logisim project Dominique_Johnson_Lab3_Milestone1.circ as structural Verilog: 5 circuits, main circuit adder_1_bit
module adder_1_bit (
  input  A,
  input  B,
  input  C_in,
  output S,
  output C_out
);

  wire and_1_out, and_2_out, and_3_out, and_4_out, and_5_out, and_6_out, and_7_out, not_1_out, not_2_out,
       not_3_out;

  not not_1 (not_1_out, A);
  not not_2 (not_2_out, B);
  not not_3 (not_3_out, C_in);
  and and_1 (and_1_out, not_1_out, not_2_out, C_in);
  and and_2 (and_2_out, not_1_out, B, not_3_out);
  and and_3 (and_3_out, A, not_2_out, not_3_out);
  and and_4 (and_4_out, A, B, C_in);
  and and_5 (and_5_out, B, C_in);
  and and_6 (and_6_out, A, C_in);
  and and_7 (and_7_out, A, B);
  or or_1 (S, and_1_out, and_2_out, and_3_out, and_4_out);
  or or_2 (C_out, and_5_out, and_6_out, and_7_out);
endmodule

module ALU_1_bit (
  input  [3:0] ALU_Ctrl,
  input  A,
  input  B,
  input  C_in,
  output R,
  output C_Out
);

  wire adder_1_bit_1_s, and_1_out, multiplexer_1_out, not_1_out, or_1_out, xor_1_out;

  Multiplexer #(.enable("false")) multiplexer_1 (.in0(B), .in1(not_1_out), .out(multiplexer_1_out), .sel(ALU_Ctrl[2]));
  not not_1 (not_1_out, B);
  and and_1 (and_1_out, A, multiplexer_1_out);
  or or_1 (or_1_out, A, multiplexer_1_out);
  xor xor_1 (xor_1_out, A, multiplexer_1_out);
  adder_1_bit adder_1_bit_1 (.A(A), .B(multiplexer_1_out), .C_in(C_in), .S(adder_1_bit_1_s), .C_out(C_Out));
  Multiplexer #(.enable("false"), .select(2)) multiplexer_2 (
    .in0(and_1_out), .in1(or_1_out), .in2(xor_1_out), .in3(adder_1_bit_1_s), .out(R), .sel(ALU_Ctrl[1:0]));
endmodule

module ALU_Control (
  input  I30,
  input  I14,
  input  I13,
  input  I12,
  input  I6,
  input  I5,
  input  I4,
  output ALU_Ctrl3,
  output ALU_Ctrl2,
  output ALU_Ctrl1,
  output ALU_Ctrl0,
  output ALU_Src
);

  wire and_2_out, not_1_out, not_2_out, not_3_out, not_4_out, not_5_out;

  not not_1 (not_1_out, I14);
  not not_2 (not_2_out, I13);
  not not_3 (not_3_out, I12);
  not not_4 (not_4_out, I5);
  not not_5 (not_5_out, I4);
  and and_1 (ALU_Ctrl2, I30, not_2_out, I5);
  or or_1 (ALU_Ctrl1, not_2_out, not_5_out);
  and and_2 (and_2_out, I13, not_3_out);
  or or_2 (ALU_Src, not_4_out, not_5_out);
  or or_3 (ALU_Ctrl0, not_1_out, and_2_out);

  assign ALU_Ctrl3 = 1'b0;
endmodule

module ALU_4_bit (
  input  [3:0] ALU_ctrl,
  input  [3:0] A,
  input  [3:0] B,
  input  C_in,
  output [3:0] R,
  output C_Out
);

  wire alu_1_bit_1_c_out, alu_1_bit_2_c_out, alu_1_bit_3_c_out;

  ALU_1_bit alu_1_bit_1 (.ALU_Ctrl(ALU_ctrl), .A(A[0]), .B(B[0]), .C_in(C_in), .R(R[0]), .C_Out(alu_1_bit_1_c_out));
  ALU_1_bit alu_1_bit_2 (
    .ALU_Ctrl(ALU_ctrl), .A(A[1]), .B(B[1]), .C_in(alu_1_bit_1_c_out), .R(R[1]), .C_Out(alu_1_bit_2_c_out));
  ALU_1_bit alu_1_bit_3 (
    .ALU_Ctrl(ALU_ctrl), .A(A[2]), .B(B[2]), .C_in(alu_1_bit_2_c_out), .R(R[2]), .C_Out(alu_1_bit_3_c_out));
  ALU_1_bit alu_1_bit_4 (.ALU_Ctrl(ALU_ctrl), .A(A[3]), .B(B[3]), .C_in(alu_1_bit_3_c_out), .R(R[3]), .C_Out(C_Out));
endmodule

module ALU_32_bit (
  input  [3:0] ALU_ctrl,
  input  C_in,
  input  [31:0] A,
  input  [31:0] B,
  output [31:0] Result,
  output C_Out
);

  wire alu_4_bit_1_c_out, alu_4_bit_2_c_out, alu_4_bit_3_c_out, alu_4_bit_4_c_out, alu_4_bit_5_c_out,
       alu_4_bit_6_c_out, alu_4_bit_7_c_out;

  ALU_4_bit alu_4_bit_1 (
    .ALU_ctrl(ALU_ctrl), .A(A[3:0]), .B(B[3:0]), .C_in(C_in), .R(Result[3:0]), .C_Out(alu_4_bit_1_c_out));
  ALU_4_bit alu_4_bit_2 (
    .ALU_ctrl(ALU_ctrl), .A(A[7:4]), .B(B[7:4]), .C_in(alu_4_bit_1_c_out), .R(Result[7:4]),
    .C_Out(alu_4_bit_2_c_out));
  ALU_4_bit alu_4_bit_3 (
    .ALU_ctrl(ALU_ctrl), .A(A[11:8]), .B(B[11:8]), .C_in(alu_4_bit_2_c_out), .R(Result[11:8]),
    .C_Out(alu_4_bit_3_c_out));
  ALU_4_bit alu_4_bit_4 (
    .ALU_ctrl(ALU_ctrl), .A(A[15:12]), .B(B[15:12]), .C_in(alu_4_bit_3_c_out), .R(Result[15:12]),
    .C_Out(alu_4_bit_4_c_out));
  ALU_4_bit alu_4_bit_5 (
    .ALU_ctrl(ALU_ctrl), .A(A[19:16]), .B(B[19:16]), .C_in(alu_4_bit_4_c_out), .R(Result[19:16]),
    .C_Out(alu_4_bit_5_c_out));
  ALU_4_bit alu_4_bit_6 (
    .ALU_ctrl(ALU_ctrl), .A(A[23:20]), .B(B[23:20]), .C_in(alu_4_bit_5_c_out), .R(Result[23:20]),
    .C_Out(alu_4_bit_6_c_out));
  ALU_4_bit alu_4_bit_7 (
    .ALU_ctrl(ALU_ctrl), .A(A[27:24]), .B(B[27:24]), .C_in(alu_4_bit_6_c_out), .R(Result[27:24]),
    .C_Out(alu_4_bit_7_c_out));
  ALU_4_bit alu_4_bit_8 (
    .ALU_ctrl(ALU_ctrl), .A(A[31:28]), .B(B[31:28]), .C_in(alu_4_bit_7_c_out), .R(Result[31:28]),
    .C_Out(C_Out));
endmodule
