// Logisim project Lab4.circ as structural Verilog: 12 circuits, main circuit adder_1_bit
module Datapath (
  input  [31:0] Instruction,
  output [31:0] out_2
);

  wire alu_control_1_alu_src, alu_control_2_alu_src, and_1_out, clock_1_out, clock_2_out, comparator_1_eq,
       control_1_branch, control_1_memread, control_1_memtoreg, control_1_memwrite, control_1_regwrite;
  wire [3:0] alu_control_1_alu_ctrl0, alu_control_2_alu_ctrl0;
  wire [7:0] register_1_q_2;
  wire [23:0] register_1_q;
  wire [31:0] adder_1_out, adder_2_out, alu_32_bit_2_result, bit_extender_1_out, data_memory_1_read_data,
       immgen_1_imm32, instruction_memory_1_instruction, multiplexer_1_out, multiplexer_2_out,
       multiplexer_3_out, multiplexer_4_out, reg_file_1_rdata1, reg_file_1_rdata2, reg_file_2_rdata1,
       reg_file_2_rdata2;

  Clock clock_1 (.out(clock_1_out));
  Register #(.width(32)) register_1 (
    .D(multiplexer_3_out), .en(1'b1), .clk(clock_2_out), .Q({register_1_q_2, register_1_q}));  // open: clr
  Clock clock_2 (.out(clock_2_out));
  assign bit_extender_1_out = {{20{Instruction[31]}}, Instruction[31:20]};  // Bit_Extender bit_extender_1
  Adder #(.width(32)) adder_1 (.a({register_1_q_2, register_1_q}), .b(32'h4), .out(adder_1_out));  // open: cin, cout
  Instruction_Memory instruction_memory_1 (
    .Address(register_1_q), .Clock_in(clock_2_out), .Instruction(instruction_memory_1_instruction));
  reg_file reg_file_1 (
    .RReg1(Instruction[19:15]), .RReg2(Instruction[24:20]), .WData(out_2), .Clock_In(clock_1_out),
    .Write(1'b1), .WReg(Instruction[11:7]), .RData1(reg_file_1_rdata1), .RData2(reg_file_1_rdata2));
  Multiplexer #(.enable("false"), .width(32)) multiplexer_1 (
    .in0(reg_file_1_rdata2), .in1(bit_extender_1_out), .out(multiplexer_1_out), .sel(alu_control_1_alu_src));
  ALU_Control alu_control_1 (
    .I30(Instruction[30]), .I14(Instruction[14]), .I13(Instruction[13]), .I12(Instruction[12]),
    .I6(Instruction[6]), .I5(Instruction[5]), .I4(Instruction[4]), .ALU_Ctrl3(alu_control_1_alu_ctrl0[3]),
    .ALU_Ctrl2(alu_control_1_alu_ctrl0[2]), .ALU_Ctrl1(alu_control_1_alu_ctrl0[1]),
    .ALU_Ctrl0(alu_control_1_alu_ctrl0[0]), .ALU_Src(alu_control_1_alu_src));
  Control control_1 (
    .I6(instruction_memory_1_instruction[6]), .I5(instruction_memory_1_instruction[5]),
    .I4(instruction_memory_1_instruction[4]), .I3(instruction_memory_1_instruction[3]),
    .I2(instruction_memory_1_instruction[2]), .I1(instruction_memory_1_instruction[1]),
    .I0(instruction_memory_1_instruction[0]), .MemToReg(control_1_memtoreg), .RegWrite(control_1_regwrite),
    .MemRead(control_1_memread), .MemWrite(control_1_memwrite), .Branch(control_1_branch));
  reg_file reg_file_2 (
    .RReg1(instruction_memory_1_instruction[19:15]), .RReg2(instruction_memory_1_instruction[24:20]),
    .WData(multiplexer_4_out), .Clock_In(clock_2_out), .Write(control_1_regwrite),
    .WReg(instruction_memory_1_instruction[11:7]), .RData1(reg_file_2_rdata1), .RData2(reg_file_2_rdata2));
  Multiplexer #(.enable("false"), .width(32)) multiplexer_2 (
    .in0(reg_file_2_rdata2), .in1(immgen_1_imm32), .out(multiplexer_2_out), .sel(alu_control_2_alu_src));
  ImmGen immgen_1 (.Instruction(instruction_memory_1_instruction), .IMM32(immgen_1_imm32));
  ALU_Control alu_control_2 (
    .I30(instruction_memory_1_instruction[30]), .I14(instruction_memory_1_instruction[14]),
    .I13(instruction_memory_1_instruction[13]), .I12(instruction_memory_1_instruction[12]),
    .I6(instruction_memory_1_instruction[6]), .I5(instruction_memory_1_instruction[5]),
    .I4(instruction_memory_1_instruction[4]), .ALU_Ctrl3(alu_control_2_alu_ctrl0[3]),
    .ALU_Ctrl2(alu_control_2_alu_ctrl0[2]), .ALU_Ctrl1(alu_control_2_alu_ctrl0[1]),
    .ALU_Ctrl0(alu_control_2_alu_ctrl0[0]), .ALU_Src(alu_control_2_alu_src));
  ALU_32_bit alu_32_bit_1 (
    .ALU_ctrl(alu_control_1_alu_ctrl0), .A(reg_file_1_rdata1), .B(multiplexer_1_out), .Result(out_2));  // open: C_Out
  ALU_32_bit alu_32_bit_2 (
    .ALU_ctrl(alu_control_2_alu_ctrl0), .A(reg_file_2_rdata1), .B(multiplexer_2_out),
    .Result(alu_32_bit_2_result));  // open: C_Out
  Adder #(.width(32)) adder_2 (
    .a({register_1_q_2, register_1_q}), .b(immgen_1_imm32), .out(adder_2_out));  // open: cin, cout
  Comparator #(.width(32)) comparator_1 (
    .a(reg_file_2_rdata1), .b(reg_file_2_rdata2), .eq(comparator_1_eq));  // open: gt, lt
  and and_1 (and_1_out, control_1_branch, comparator_1_eq);
  Multiplexer #(.enable("false"), .width(32)) multiplexer_3 (
    .in0(adder_1_out), .in1(adder_2_out), .out(multiplexer_3_out), .sel(and_1_out));
  Data_Memory data_memory_1 (
    .Address(alu_32_bit_2_result[25:0]), .MemWrite(control_1_memwrite), .MemRead(control_1_memread),
    .Clock_In(clock_2_out), .Write_Data(reg_file_2_rdata2), .Read_Data(data_memory_1_read_data));
  Multiplexer #(.enable("false"), .width(32)) multiplexer_4 (
    .in0(alu_32_bit_2_result), .in1(data_memory_1_read_data), .out(multiplexer_4_out),
    .sel(control_1_memtoreg));
endmodule

module adder_1_bit (
  input  A,
  input  B,
  input  C_in,
  output S,
  output C_out
);

  wire and_1_out, and_2_out, and_3_out, and_4_out, and_5_out, and_6_out, and_7_out, not_1_out, not_2_out,
       not_3_out;

  not not_1 (not_1_out, A);
  not not_2 (not_2_out, B);
  not not_3 (not_3_out, C_in);
  and and_1 (and_1_out, not_1_out, not_2_out, C_in);
  and and_2 (and_2_out, not_1_out, B, not_3_out);
  and and_3 (and_3_out, A, not_2_out, not_3_out);
  and and_4 (and_4_out, A, B, C_in);
  and and_5 (and_5_out, B, C_in);
  and and_6 (and_6_out, A, C_in);
  and and_7 (and_7_out, A, B);
  or or_1 (S, and_1_out, and_2_out, and_3_out, and_4_out);
  or or_2 (C_out, and_5_out, and_6_out, and_7_out);
endmodule

module ALU_1_bit (
  input  [3:0] ALU_Ctrl,
  input  A,
  input  B,
  input  C_in,
  output R,
  output C_Out
);

  wire adder_1_bit_1_s, and_1_out, multiplexer_1_out, not_1_out, or_1_out, xor_1_out;

  Multiplexer #(.enable("false")) multiplexer_1 (.in0(B), .in1(not_1_out), .out(multiplexer_1_out), .sel(ALU_Ctrl[2]));
  not not_1 (not_1_out, B);
  and and_1 (and_1_out, A, multiplexer_1_out);
  or or_1 (or_1_out, A, multiplexer_1_out);
  xor xor_1 (xor_1_out, A, multiplexer_1_out);
  adder_1_bit adder_1_bit_1 (.A(A), .B(multiplexer_1_out), .C_in(C_in), .S(adder_1_bit_1_s), .C_out(C_Out));
  Multiplexer #(.enable("false"), .select(2)) multiplexer_2 (
    .in0(and_1_out), .in1(or_1_out), .in2(xor_1_out), .in3(adder_1_bit_1_s), .out(R), .sel(ALU_Ctrl[1:0]));
endmodule

module ALU_Control (
  input  I30,
  input  I14,
  input  I13,
  input  I12,
  input  I6,
  input  I5,
  input  I4,
  output ALU_Ctrl3,
  output ALU_Ctrl2,
  output ALU_Ctrl1,
  output ALU_Ctrl0,
  output ALU_Src
);

  wire and_2_out, not_1_out, not_2_out, not_3_out, not_4_out, not_5_out;

  not not_1 (not_1_out, I14);
  not not_2 (not_2_out, I13);
  not not_3 (not_3_out, I12);
  not not_4 (not_4_out, I5);
  not not_5 (not_5_out, I4);
  and and_1 (ALU_Ctrl2, I30, not_2_out, I5);
  or or_1 (ALU_Ctrl1, not_2_out, not_5_out);
  and and_2 (and_2_out, I13, not_3_out);
  or or_2 (ALU_Src, not_4_out, not_5_out);
  or or_3 (ALU_Ctrl0, not_1_out, and_2_out);

  assign ALU_Ctrl3 = 1'b0;
endmodule

module ALU_4_bit (
  input  [3:0] ALU_ctrl,
  input  [3:0] A,
  input  [3:0] B,
  input  C_in,
  output [3:0] R,
  output C_Out
);

  wire alu_1_bit_1_c_out, alu_1_bit_2_c_out, alu_1_bit_3_c_out;

  ALU_1_bit alu_1_bit_1 (.ALU_Ctrl(ALU_ctrl), .A(A[0]), .B(B[0]), .C_in(C_in), .R(R[0]), .C_Out(alu_1_bit_1_c_out));
  ALU_1_bit alu_1_bit_2 (
    .ALU_Ctrl(ALU_ctrl), .A(A[1]), .B(B[1]), .C_in(alu_1_bit_1_c_out), .R(R[1]), .C_Out(alu_1_bit_2_c_out));
  ALU_1_bit alu_1_bit_3 (
    .ALU_Ctrl(ALU_ctrl), .A(A[2]), .B(B[2]), .C_in(alu_1_bit_2_c_out), .R(R[2]), .C_Out(alu_1_bit_3_c_out));
  ALU_1_bit alu_1_bit_4 (.ALU_Ctrl(ALU_ctrl), .A(A[3]), .B(B[3]), .C_in(alu_1_bit_3_c_out), .R(R[3]), .C_Out(C_Out));
endmodule

module ALU_32_bit (
  input  [3:0] ALU_ctrl,
  input  [31:0] A,
  input  [31:0] B,
  output [31:0] Result,
  output C_Out
);

  wire alu_4_bit_1_c_out, alu_4_bit_2_c_out, alu_4_bit_3_c_out, alu_4_bit_4_c_out, alu_4_bit_5_c_out,
       alu_4_bit_6_c_out, alu_4_bit_7_c_out;

  ALU_4_bit alu_4_bit_1 (
    .ALU_ctrl(ALU_ctrl), .A(A[3:0]), .B(B[3:0]), .R(Result[3:0]), .C_Out(alu_4_bit_1_c_out));  // open: C_in
  ALU_4_bit alu_4_bit_2 (
    .ALU_ctrl(ALU_ctrl), .A(A[7:4]), .B(B[7:4]), .C_in(alu_4_bit_1_c_out), .R(Result[7:4]),
    .C_Out(alu_4_bit_2_c_out));
  ALU_4_bit alu_4_bit_3 (
    .ALU_ctrl(ALU_ctrl), .A(A[11:8]), .B(B[11:8]), .C_in(alu_4_bit_2_c_out), .R(Result[11:8]),
    .C_Out(alu_4_bit_3_c_out));
  ALU_4_bit alu_4_bit_4 (
    .ALU_ctrl(ALU_ctrl), .A(A[15:12]), .B(B[15:12]), .C_in(alu_4_bit_3_c_out), .R(Result[15:12]),
    .C_Out(alu_4_bit_4_c_out));
  ALU_4_bit alu_4_bit_5 (
    .ALU_ctrl(ALU_ctrl), .A(A[19:16]), .B(B[19:16]), .C_in(alu_4_bit_4_c_out), .R(Result[19:16]),
    .C_Out(alu_4_bit_5_c_out));
  ALU_4_bit alu_4_bit_6 (
    .ALU_ctrl(ALU_ctrl), .A(A[23:20]), .B(B[23:20]), .C_in(alu_4_bit_5_c_out), .R(Result[23:20]),
    .C_Out(alu_4_bit_6_c_out));
  ALU_4_bit alu_4_bit_7 (
    .ALU_ctrl(ALU_ctrl), .A(A[27:24]), .B(B[27:24]), .C_in(alu_4_bit_6_c_out), .R(Result[27:24]),
    .C_Out(alu_4_bit_7_c_out));
  ALU_4_bit alu_4_bit_8 (
    .ALU_ctrl(ALU_ctrl), .A(A[31:28]), .B(B[31:28]), .C_in(alu_4_bit_7_c_out), .R(Result[31:28]),
    .C_Out(C_Out));
endmodule

module reg_file_4 (
  input  [1:0] RReg1,
  input  [1:0] RReg2,
  input  [31:0] WData,
  input  Clock_in,
  input  Write,
  input  [1:0] WReg,
  output [31:0] RData1,
  output [31:0] RData2
);

  wire demultiplexer_1_out0, demultiplexer_1_out1, demultiplexer_1_out2, demultiplexer_1_out3;
  wire [31:0] register_1_q, register_2_q, register_3_q, register_4_q;

  Demultiplexer #(.enable("false"), .select(2)) demultiplexer_1 (
    .out0(demultiplexer_1_out0), .out1(demultiplexer_1_out1), .out2(demultiplexer_1_out2),
    .out3(demultiplexer_1_out3), .in(Write), .sel(WReg));
  Register #(.width(32)) register_1 (
    .D(WData), .en(demultiplexer_1_out0), .clk(Clock_in), .Q(register_1_q), .clr(Write));
  Register #(.width(32)) register_2 (
    .D(WData), .en(demultiplexer_1_out1), .clk(Clock_in), .Q(register_2_q));  // open: clr
  Register #(.width(32)) register_3 (
    .D(WData), .en(demultiplexer_1_out2), .clk(Clock_in), .Q(register_3_q));  // open: clr
  Register #(.width(32)) register_4 (
    .D(WData), .en(demultiplexer_1_out3), .clk(Clock_in), .Q(register_4_q));  // open: clr
  Multiplexer #(.enable("false"), .select(2), .width(32)) multiplexer_1 (
    .in0(register_1_q), .in1(register_2_q), .in2(register_3_q), .in3(register_4_q), .out(RData1), .sel(RReg1));
  Multiplexer #(.enable("false"), .select(2), .width(32)) multiplexer_2 (
    .in0(register_1_q), .in1(register_2_q), .in2(register_3_q), .in3(register_4_q), .out(RData2), .sel(RReg2));
endmodule

module reg_file (
  input  [4:0] RReg1,
  input  [4:0] RReg2,
  input  [31:0] WData,
  input  Clock_In,
  input  Write,
  input  [4:0] WReg,
  output [31:0] RData1,
  output [31:0] RData2
);

  wire R1, R2, R3, R4, R5, R6, R7, R8, R9, R10, R11, R12, R13, R14, R15, R16, R17, R18, R19, R20, R21, R22,
       R23, R24, R25, R26, R27, R28, R29, R30, R31, R32;
  wire [31:0] Q1, Q2, Q3, Q4, Q5, Q6, Q7, Q8, Q9, Q10, Q11, Q12, Q13, Q14, Q15, Q16, Q17, Q18, Q19, Q20, Q21,
       Q22, Q23, Q24, Q25, Q26, Q27, Q28, Q29, Q30, Q31, Q32;

  Demultiplexer #(.enable("false"), .select(5)) demultiplexer_1 (
    .out0(R1), .out1(R2), .out2(R3), .out3(R4), .out4(R5), .out5(R6), .out6(R7), .out7(R8), .out8(R9),
    .out9(R10), .out10(R11), .out11(R12), .out12(R13), .out13(R14), .out14(R15), .out15(R16), .out16(R17),
    .out17(R18), .out18(R19), .out19(R20), .out20(R21), .out21(R22), .out22(R23), .out23(R24), .out24(R25),
    .out25(R26), .out26(R27), .out27(R28), .out28(R29), .out29(R30), .out30(R31), .out31(R32), .in(Write),
    .sel(WReg));
  Register #(.width(32)) register_1 (.D(WData), .en(R1), .clk(Clock_In), .Q(Q1), .clr(Write));
  Register #(.width(32)) register_2 (.D(WData), .en(R2), .Q(Q2));  // open: clk, clr
  Register #(.width(32)) register_3 (.en(R3), .clk(Clock_In), .Q(Q3));  // open: D, clr
  Register #(.width(32)) register_4 (.D(WData), .en(R4), .clk(Clock_In), .Q(Q4));  // open: clr
  Register #(.width(32)) register_5 (.D(WData), .en(R5), .clk(Clock_In), .Q(Q5));  // open: clr
  Register #(.width(32)) register_6 (.D(WData), .en(R6), .clk(Clock_In), .Q(Q6));  // open: clr
  Register #(.width(32)) register_7 (.D(WData), .en(R7), .clk(Clock_In), .Q(Q7));  // open: clr
  Register #(.width(32)) register_8 (.D(WData), .en(R8), .clk(Clock_In), .Q(Q8));  // open: clr
  Register #(.width(32)) register_9 (.D(WData), .en(R9), .clk(Clock_In), .Q(Q9));  // open: clr
  Register #(.width(32)) register_10 (.D(WData), .en(R10), .clk(Clock_In), .Q(Q10));  // open: clr
  Register #(.width(32)) register_11 (.D(WData), .en(R11), .clk(Clock_In), .Q(Q11));  // open: clr
  Register #(.width(32)) register_12 (.D(WData), .en(R12), .clk(Clock_In), .Q(Q12));  // open: clr
  Register #(.width(32)) register_13 (.D(WData), .en(R13), .clk(Clock_In), .Q(Q13));  // open: clr
  Register #(.width(32)) register_14 (.D(WData), .en(R14), .clk(Clock_In), .Q(Q14));  // open: clr
  Register #(.width(32)) register_15 (.D(WData), .en(R15), .clk(Clock_In), .Q(Q15));  // open: clr
  Register #(.width(32)) register_16 (.D(WData), .en(R16), .clk(Clock_In), .Q(Q16));  // open: clr
  Register #(.width(32)) register_17 (.D(WData), .en(R17), .clk(Clock_In), .Q(Q17));  // open: clr
  Register #(.width(32)) register_18 (.D(WData), .en(R18), .clk(Clock_In), .Q(Q18));  // open: clr
  Register #(.width(32)) register_19 (.D(WData), .en(R19), .clk(Clock_In), .Q(Q19));  // open: clr
  Register #(.width(32)) register_20 (.D(WData), .en(R20), .clk(Clock_In), .Q(Q20));  // open: clr
  Register #(.width(32)) register_21 (.D(WData), .en(R21), .clk(Clock_In), .Q(Q21));  // open: clr
  Register #(.width(32)) register_22 (.D(WData), .en(R22), .clk(Clock_In), .Q(Q22));  // open: clr
  Register #(.width(32)) register_23 (.D(WData), .en(R23), .clk(Clock_In), .Q(Q23));  // open: clr
  Register #(.width(32)) register_24 (.D(WData), .en(R24), .clk(Clock_In), .Q(Q24));  // open: clr
  Register #(.width(32)) register_25 (.D(WData), .en(R25), .clk(Clock_In), .Q(Q25));  // open: clr
  Register #(.width(32)) register_26 (.D(WData), .en(R26), .clk(Clock_In), .Q(Q26));  // open: clr
  Register #(.width(32)) register_27 (.D(WData), .en(R27), .clk(Clock_In), .Q(Q27));  // open: clr
  Register #(.width(32)) register_28 (.D(WData), .en(R28), .clk(Clock_In), .Q(Q28));  // open: clr
  Register #(.width(32)) register_29 (.D(WData), .en(R29), .clk(Clock_In), .Q(Q29));  // open: clr
  Register #(.width(32)) register_30 (.D(WData), .en(R30), .clk(Clock_In), .Q(Q30));  // open: clr
  Register #(.width(32)) register_31 (.D(WData), .en(R31), .clk(Clock_In), .Q(Q31));  // open: clr
  Register #(.width(32)) register_32 (.D(WData), .en(R32), .clk(Clock_In), .Q(Q32));  // open: clr
  Multiplexer #(.enable("false"), .select(5), .width(32)) multiplexer_1 (
    .in0(Q1), .in1(Q2), .in2(Q3), .in3(Q4), .in4(Q5), .in5(Q6), .in6(Q7), .in7(Q8), .in8(Q9), .in9(Q10),
    .in10(Q11), .in11(Q12), .in12(Q13), .in13(Q14), .in14(Q15), .in15(Q16), .in16(Q17), .in17(Q18),
    .in18(Q19), .in19(Q20), .in20(Q21), .in21(Q22), .in22(Q23), .in23(Q24), .in24(Q25), .in25(Q26),
    .in26(Q27), .in27(Q28), .in28(Q29), .in29(Q30), .in30(Q31), .in31(Q32), .out(RData1), .sel(RReg1));
  Multiplexer #(.enable("false"), .select(5), .width(32)) multiplexer_2 (
    .in0(Q1), .in1(Q2), .in2(Q3), .in3(Q4), .in4(Q5), .in5(Q6), .in6(Q7), .in7(Q8), .in8(Q9), .in9(Q10),
    .in10(Q11), .in11(Q12), .in12(Q13), .in13(Q14), .in14(Q15), .in15(Q16), .in16(Q17), .in17(Q18),
    .in18(Q19), .in19(Q20), .in20(Q21), .in21(Q22), .in22(Q23), .in23(Q24), .in24(Q25), .in25(Q26),
    .in26(Q27), .in27(Q28), .in28(Q29), .in29(Q30), .in30(Q31), .in31(Q32), .out(RData2), .sel(RReg2));
endmodule

module ImmGen (
  input  [31:0] Instruction,
  output [31:0] IMM32
);

  Multiplexer #(.enable("false"), .width(4)) multiplexer_1 (
    .in0(Instruction[24:21]), .in1(Instruction[11:8]), .out(IMM32[4:1]), .sel(Instruction[5]));
  Multiplexer #(.enable("false"), .select(2)) multiplexer_2 (
    .in0(Instruction[20]), .in1(Instruction[7]), .in3(1'b0), .out(IMM32[0]), .sel(Instruction[6:5]));  // open: in2
  Multiplexer #(.enable("false")) multiplexer_3 (
    .in0(Instruction[31]), .in1(Instruction[7]), .out(IMM32[11]), .sel(Instruction[6]));
  assign IMM32[31:12] = {{19{Instruction[31]}}, Instruction[31]};  // Bit_Extender bit_extender_1

  assign IMM32[10:5] = Instruction[30:25];

  // Other names for the same wires on the sheet: I30_25[5:0] = Instruction[30:25]; I5 = Instruction[5];
  //   I6_5[1:0] = Instruction[6:5]; I6 = Instruction[6]; I7 = Instruction[7]; I11_8[3:0] = Instruction[11:8];
  //   I20 = Instruction[20]; I24_21[3:0] = Instruction[24:21]; I31 = Instruction[31]
endmodule

module Control (
  input  I6,
  input  I5,
  input  I4,
  input  I3,
  input  I2,
  input  I1,
  input  I0,
  output MemToReg,
  output RegWrite,
  output MemRead,
  output MemWrite,
  output Branch
);

  wire not_1_out, not_2_out;

  not not_1 (not_1_out, I6);
  not not_2 (not_2_out, I5);
  not not_3 (MemToReg, I4);
  or or_1 (RegWrite, not_2_out, I4);
  and and_1 (MemRead, not_2_out, MemToReg);
  and and_2 (MemWrite, not_1_out, I5, MemToReg);

  assign Branch = I6;
endmodule

module Instruction_Memory (
  input  [23:0] Address,
  input  Clock_in,
  output [31:0] Instruction
);

  wire not_1_out;

  not not_1 (not_1_out, Clock_in);
  RAM #(.addrWidth(22), .asyncread("true"), .dataWidth(32)) ram_1 (
    .addr(Address[23:2]), .we(1'b0), .oe(not_1_out), .dout(Instruction));  // open: clk, din
endmodule

module Data_Memory (
  input  [25:0] Address,
  input  MemWrite,
  input  MemRead,
  input  Clock_In,
  input  [31:0] Write_Data,
  output [31:0] Read_Data
);

  RAM #(.addrWidth(24), .dataWidth(32)) ram_1 (
    .addr(Address[25:2]), .we(MemWrite), .oe(MemRead), .clk(Clock_In), .din(Write_Data), .dout(Read_Data));
endmodule
